# Fritzing sketch Smart room fritzing (saved by Fritzing 0.9.4)
breadboards: 2

parts:
  Teensy_3_1 = Teensy 3.1
  GY1 = MPU-6050 Board GY-521 [form="♀ (female)" package=THT]
  S1 = Pushbutton [package="[THT]"]
  S2 = Pushbutton [package="[THT]"]
  Part1 = 12 NeoPixel Ring [part_number=1643]
  M1 = BMP280
  RG_encoder1 = SprkFn RG Encoder [package="DIP (Dual Inline) [THT]"]
  WIZ820io1 = WIZ820io [part_number=WIZ820io]
  R1 = Resistor [tolerance=±5% resistance=220 package=THT]
  R2 = Resistor [tolerance=±5% resistance=220 package=THT]
  OLED_I2C1 = OLED 128x64 I2C Monochrome Display

nets:
  N1: Teensy_3_1.D0, S2.Pin_3, S2.Pin_4
  N2: Teensy_3_1.D10, WIZ820io1.nSS
  N3: Teensy_3_1.D11, WIZ820io1.MISO
  N4: Teensy_3_1.D12, WIZ820io1.MOSI
  N5: Teensy_3_1.D13, WIZ820io1.SCLK
  N6: Teensy_3_1.A3/D17, Part1.IN
  N7: Teensy_3_1.A4/D18, GY1.pin3, M1.SCL, OLED_I2C1.SCK
  N8: Teensy_3_1.A5/D19, GY1.pin4, M1.SDA, OLED_I2C1.SDA
  N9: Teensy_3_1.A8/D22, RG_encoder1.C
  N10: Teensy_3_1.A9/D23, RG_encoder1.A
  3V3: Teensy_3_1.3V3, WIZ820io1.VIN
  VIN: Teensy_3_1.Vin, GY1.pin1, S1.Pin_1, S1.Pin_2, S2.Pin_1, S2.Pin_2, Part1.VDD, M1.VIN, R2.Pin_1, OLED_I2C1.VDD
  GND: GY1.pin2, Part1.GND, M1.GND, RG_encoder1.B, WIZ820io1.GND, R1.Pin_0, R2.Pin_0, OLED_I2C1.GND
  N11: S1.Pin_3, S1.Pin_4, R1.Pin_1

custom parts:
  MPU-6050 Board GY-521: Acelerometro y Giroscopio MPU-6050 Board GY-521
  Pushbutton: A generic pushbutton.
  12 NeoPixel Ring: 12 ultra bright smart LED NeoPixels are arranged in a circle with 1.5" (37mm) outer diameter. The rings are 'chainable' - connect the output pin of one to the input pin of another. Use only one microcontroller pin to control as many as you can chain together! Each LED is addressable as the driver chip is inside the LED. Each one has ~18mA constant current drive so the color will be very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
  BMP280: Temperature Humidity Barometric presure Sensor, I2C
  SprkFn RG Encoder: SparkFun RG Rotary Encoder
